# Fritzing sketch smart_light (saved by Fritzing 0.9.2b)

parts:
  Part1 = Arduino Pro Mini v13
  PIR1 = PIR sensor
  neopixel1 = Neopixel Ring 12
  RF1 = nRF8001 Bluetooth LE Breakout
  Power_plug1 = Power plug
  U1 = Voltage Regulator - 5V [package="TO220 [THT]"]
  U2 = IC, SIP package, 7 pins [chip_label=TSL2561]

nets:
  N1: Part1.A4, U2.pin6
  N2: Part1.A5, U2.pin7
  GND: Part1.GND, PIR1.GND, neopixel1.GND, RF1.GND, Power_plug1.GND, U1.GND, U2.pin2
  VCC: Part1.VCC, PIR1.VDD, neopixel1.VCC, RF1.VIN, U1.output_voltage, U2.pin1
  N3: Part1.D13/SCK, RF1.SCK
  N4: Part1.D12/MISO, RF1.MISO
  N5: Part1.D11_PWM/MOSI, RF1.MOSI
  N6: Part1.D10_PWM/SS, RF1.REQ
  N7: Part1.D9_PWM, RF1.RST
  N8: Part1.D6_PWM, neopixel1.IN
  N9: Part1.D3_PWM, PIR1.SIG
  N10: Part1.D2, RF1.RDY
  N11: Power_plug1.VCC, U1.input_voltage

notes:
  Smart Light v1.0.0
  http://j.mp/smart-light

custom parts:
  Neopixel Ring 12: Neopixel Ring x12
  nRF8001 Bluetooth LE Breakout: nRF8001 Breakout Board
